// Digital circuit core.dig as structural Verilog
module core (
  input  clk,
  output [31:0] out
);

  wire A, alu, AluASrc, and_1_out, B, branch_1_p4, demultiplexer_1_out_1, imm, need_imm, pc_1_p1, r1Data,
       r2Data;
  wire [2:0] funct3, immOp;
  wire [3:0] alu_op, BranchOp;
  wire [4:0] rd, rs1, rs2;
  wire [6:0] funct7, opcode;
  wire [31:0] AluOut, DataRd, pc_1_p3, sum_s;

  // PC pc_1: pin names not known; wires that end beside it: pc_1_p1, clk, pc_1_p3
  Add #(.Bits(32)) sum (.a(pc_1_p3), .b(32'h4), .c_i(1'b0), .s(sum_s));  // open: c_o
  Insts_Memory insts_memory_1 (.pc(pc_1_p3), .out({funct7, rs2, rs1, funct3, rd, opcode}));
  control_unit control_unit_1 (
    .opcode(opcode), .funct3(funct3), .funct7(funct7), .alu_op(alu_op), .alu(alu), .need_imm(need_imm),
    .immOp(immOp), .AluASrc(AluASrc), .BranchOp(BranchOp));
  register_unit register_unit_1 (
    .rdData(DataRd), .rs1(rs1), .rs2(rs2), .rd(rd), .clk(clk), .enable(1'b0));  // open: rs1Data, rs2Data
  // ImmGenerator immgenerator_1: pin names not known; wires that end beside it: {funct7, rs2, rs1, funct3, rd}, immOp, r1Data, r2Data, imm
  Demultiplexer demultiplexer_1 (.sel(alu), .in(1'b1), .out_1(demultiplexer_1_out_1));  // open: out_0
  // Branch branch_1: pin names not known; wires that end beside it: r1Data, r2Data, BranchOp, branch_1_p4
  and and_1 (and_1_out, need_imm, demultiplexer_1_out_1);
  Multiplexer multiplexer_1 (.sel(AluASrc), .in_0(r1Data), .in_1(pc_1_p3[0]), .out(A));
  Multiplexer multiplexer_2 (.sel(and_1_out), .in_0(r2Data), .in_1(imm), .out(B));
  Multiplexer multiplexer_3 (.sel(branch_1_p4), .in_0(sum_s[0]), .in_1(AluOut[0]), .out(pc_1_p1));
  // ALU alu_1: pin names not known; wires that end beside it: A, B, alu_op, AluOut
  Multiplexer #(.Bits(32), .Selector_Bits(2)) multiplexer_4 (
    .in_0(AluOut), .in_1(sum_s), .out(DataRd));  // open: sel, in_2, in_3
  // Pins of 1 and 32 bits meet at pc_1_p3
  // Pins of 1 and 32 bits meet at sum_s
  // Pins of 1 and 32 bits meet at AluOut
endmodule
